# Fritzing sketch schema-read-rfid (saved by Fritzing 0.9.2b)

parts:
  Raspberry_Pi1 = Raspberry Pi 2
  Composant2 = RFID-RC522-v3

nets:
  3V3: Raspberry_Pi1.3V3, Composant2.3.3V
  N1: Raspberry_Pi1.GPIO10, Composant2.MOSI
  N2: Raspberry_Pi1.GPIO9, Composant2.MISO
  N3: Raspberry_Pi1.GPIO11, Composant2.SCK
  N4: Raspberry_Pi1.GPIO8, Composant2.SDA
  N5: Raspberry_Pi1.GPIO25, Composant2.RST
  GND: Raspberry_Pi1.GND, Composant2.GND
  N6: Raspberry_Pi1.GPIO24, Composant2.IRQ

custom parts:
  RFID-RC522-v3: A simple China made RFID-RC522 Reader (6x4 cm); do check the pin labels, as this is a MFRC522 based clone.
